# Fritzing sketch JAMMER WIFI (saved by Fritzing 0.9.3b)
circuit board: 9.60373cm x 5.5887cm

parts:
  OLED_I2C1 = OLED 128x64 I2C NEW
  Part1 = Arduino Nano (Rev3.0)
  S1 = Pushbutton [package="[SMD]"]
  Part2 = NRF24L01+ Breakout Board
  S2 = Pushbutton [package="[SMD]"]
  S3 = Pushbutton [package="[SMD]"]
  S4 = Pushbutton [package="[SMD]"]
  JP1 = Header 6 [package=molex-1x6-ra]
  JP2 = Header 2 [package=springterminal-2.54mm-2]

nets:
  N1: OLED_I2C1.SDA, Part1.A4
  N2: OLED_I2C1.SCK, Part1.A5
  GND: OLED_I2C1.GND, Part1.GND, S4.Pin_3, S4.Pin_4, JP1.1, JP1.6, JP2.2
  VCC: OLED_I2C1.VCC, Part1.5V
  N3: Part1.D2, S2.Pin_2
  N4: Part1.D3, S1.Pin_2
  N5: Part1.D4, S3.Pin_2
  N6: Part1.D6, S4.Pin_1, S4.Pin_2
  N7: Part1.D9, Part2.CE
  N8: Part1.D10, Part2.CS
  N9: Part1.D11/MOSI, Part2.MOSI
  N10: Part1.D12/MISO, Part2.MISO
  N11: Part1.VIN, JP2.1
  3V3: Part1.3V3, Part2.VCC
  N12: Part1.D13/SCK, Part2.SCK
  N13: S1.Pin_3, S1.Pin_4, JP1.3
  N14: Part2.GND, JP1.5
  N15: S2.Pin_4, JP1.4
  N16: S3.Pin_4, JP1.2

custom parts:
  OLED 128x64 I2C NEW: OLED 128x64 I2C Monochrome Display
